# Fritzing sketch Project_2 (saved by Fritzing 0.9.2b)
breadboards: 1

parts:
  Uno = Arduino Uno (Rev3)
  Ultrasonic_Range_Finder = SRF05 Ultrasonic Rangefinder
  J1 = Basic Servo
  J2 = Basic Servo
  Raspberry_Pi2 = Raspberry Pi 2
  DHT11 = Humidity and Temperature Sensor RHT03
  R1 = Resistor [tolerance=±5% resistance=10k package=THT]

nets:
  N1: Uno.A4/SDA, Raspberry_Pi2.GPIO3
  N2: Uno.A5/SCL, Raspberry_Pi2.GPIO2
  N3: Uno.D11_PWM/MOSI, Ultrasonic_Range_Finder.Trig
  N4: Uno.D12/MISO, Ultrasonic_Range_Finder.Echo
  GND: Uno.GND, Ultrasonic_Range_Finder.GND, J1.gnd, J2.gnd, Raspberry_Pi2.GND, DHT11.GND_2
  N5: Uno.D2, DHT11.Data-signal, R1.Pin_0
  N6: Uno.D3_PWM, J1.pulse
  N7: Uno.D5_PWM, J2.pulse
  VCC: Uno.5V, Ultrasonic_Range_Finder.VCC, J1.vcc, J2.vcc, DHT11.Vcc, R1.Pin_1
